# Fritzing sketch shpritz (saved by Fritzing 0.9.3b)
breadboards: 1

parts:
  Q1 = MOSFET-NCHANNEL [package=to220v]
  D1 = Diode [package=diode-1n4148]  # not connected
  hc-sr1 = hc-sr04
  Part1 = Arduino Uno (Rev3) - ICSP
  R1 = Resistor [tolerance=±5% resistance=220 package="0603 [SMD]"]
  VCC1 = Battery
  M1 = DC Motor

nets:
  N1: Q1.G, R1.Pin_1
  N2: Q1.D, M1.pin_2
  GND: Q1.S, hc-sr1.GND, Part1.GND, VCC1.-
  VCC: hc-sr1.VCC, Part1.5V
  N3: hc-sr1.Trig, Part1.D8
  N4: hc-sr1.Echo, Part1.D9_PWM
  N5: Part1.D10_PWM/SS, R1.Pin_0
